# Fritzing sketch ec_ph_esp32 (saved by Fritzing 0.9.3b)

parts:
  EC-Salinity_Probe_Interface1 = EC-Salinity Probe Interface [chip_label="EC-Salinity Probe Interface" package="DIP (Dual Inline) [THT]"]
  U1 = ESP32S-HiLetgo [part_number=ESP32S-HiLetgo]
  IC1 = DIP - 8 pins [chip_label="uFire ISE Probe Interface" package="DIP (Dual Inline) [THT]"]

nets:
  VCC: EC-Salinity_Probe_Interface1.VCC, U1.3.3, IC1.VCC
  N1: EC-Salinity_Probe_Interface1.SCL, U1.GPIO33, IC1.SCL
  N2: EC-Salinity_Probe_Interface1.SDA, U1.GPIO19, IC1.SDA
  GND: EC-Salinity_Probe_Interface1.GND, U1.GND, IC1.GND

custom parts:
  ESP32S-HiLetgo: HiLetgo ESP-WROOM-32 ESP32 ESP-32S Development Board 2.4GHz Dual-Mode WiFi + Bluetooth Dual Cores Microcontroller The ESP32 integrated with Antenna switches, RF Balun, power amplifiers, low-noise amplifiers, filters, and management modules, and the entire solution occupies the least area of PCB. 2.4 GHz Wi-Fi plus Bluetooth dual-mode chip, with TSMC Ultra-low power consumption 40nm technology,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
  DIP - 8 pins: A DIP stand-in part for whatever IC you want. With 8 pins on a 300mil dual inline package (DIP) footprint.
